# Fritzing sketch PulseGen (saved by Fritzing 0.9.3b)
circuit board: 8.46667cm x 5.64444cm
breadboards: 1

parts:
  Teensy1 = Teensy 3.6 (Basic)
  S1 = Round Pushbutton
  U1 = BNC [package=bnc]
  U2 = BNC [package=bnc]
  Pot = POT [package=3362u]
  LED1 = smd LED [color="Red (633nm)" package="0805 [SMD]"]
  LCD = Standard LCD 16x2 white on blue [part_number=181]
  Keypad4x1 = Keypad Membran 4x4
  IC1 = IC, DIP package, 8 pins [chip_label=TLP2530]

nets (from the breadboard view):
  GND: Teensy1.GND, Teensy1.GND1, S1.leg0, U2.GND, Pot.E, LED1.cathode, LCD.VSS, LCD.R/W, LCD.LED-, IC1.pin5
  N1: Teensy1.D2, LCD.DB7
  N2: Teensy1.D3, LCD.DB6
  N3: Teensy1.D4, LCD.DB5
  N4: Teensy1.D5, LCD.DB4
  N5: Teensy1.D6, IC1.pin7
  N6: Teensy1.D7, S1.leg1
  N7: Teensy1.D8, LED1.anode
  N8: Teensy1.D9, LCD.E
  N9: Teensy1.D10, LCD.RS
  N10: Teensy1.A2/D16, Keypad4x1.Pin1
  N11: Teensy1.A3/D17, Keypad4x1.Pin2
  N12: Teensy1.A4/D18, Keypad4x1.Pin3
  N13: Teensy1.A5/D19, Keypad4x1.Pin4
  N14: Teensy1.A6/D20, Keypad4x1.Pin5
  N15: Teensy1.A7/D21, Keypad4x1.Pin6
  N16: Teensy1.A8/D22, Keypad4x1.Pin7
  N17: Teensy1.A9/D23, Keypad4x1.Pin8
  N18: Teensy1.3V3, Teensy1.3V3_1
  VIN: Teensy1.Vin, Pot.A, LCD.VDD, LCD.LED+, IC1.pin8
  N19: Teensy1.D29, U2.OUT
  N20: U1.GND, IC1.pin2
  N21: U1.OUT, IC1.pin1
  N22: Pot.S, LCD.V0

custom parts:
  Teensy 3.6 (Basic): The Teensy is a complete USB-based microcontoller development system, in a very small footprint, capable of implementing many types of projects. All programming is done via the USB port. No special programmer is needed, only a standard micro-USB cable and a PC or Macintosh with a USB port.
  Standard LCD 16x2 white on blue: Standard HD44780 LCDs are useful for creating standalone projects. * 16 characters wide, 2 rows * White text on blue background * Connection port is 0.1" pitch, single row for easy breadboarding and wiring
  Keypad Membran 4x4: Membrane Keypad 4x4 Matrix
